# Fritzing sketch Vdetect (saved by Fritzing 0.9.5d)

parts:
  SG2 = Buzzer 12mm [package=buzzer-12mm-ns]
  R3 = Resistor [tolerance=±5% resistance=220 package=THT]
  R4 = Resistor [tolerance=±5% resistance=10k package=THT]
  Part3 = InvenSense MPU6050
  esp2 = ESP32 DevKitc V4
  M2 = NEO-6M GPS Module [part_number=GY-GPS6MV2]
  A7680C1 = SIM800L BO
  LED2 = LED - 5mm [color="Red (633nm)" package="5 mm [THT]"]
  S2 = Round Pushbutton
  Bat_5v = Lilypad Power Supply

nets:
  GND: SG2.1, R3.Pin_0, Part3.GND, esp2.GND, M2.GND, A7680C1.pin_6, S2.leg1, Bat_5v.GND
  N1: SG2.2, esp2.IO18
  N2: R3.Pin_1, LED2.cathode
  N3: R4.Pin_0, esp2.IO4
  N4: R4.Pin_1, S2.leg0
  VCC: Part3.VCC, esp2.5V, M2.Vcc, A7680C1.PIN2, Bat_5v.+
  N5: Part3.SCL, esp2.IO22
  N6: Part3.SDA, esp2.IO21
  N7: esp2.IO16, M2.Tx
  N8: esp2.IO17, M2.Rx
  N9: esp2.IO19, LED2.anode
  N10: esp2.IO26, A7680C1.pin_5
  N11: esp2.IO27, A7680C1.pin_4

custom parts:
  ESP32 DevKitc V4: ESP32-DevKitC board with ESP32-WROOM-32 module. ESP32-DevKitC V4 is a small-sized ESP32-based development board produced by Espressif. Most of the pins on the ESP module are broken out to the pin headers on the board. The pins D0, D1, D2, D3, CMD and CLK are used internally for communication between ESP32 and SPI flash memory. They are grouped on both sides near the USB connector. Avoid using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
  NEO-6M GPS Module: GY-GPS6MV2 NEO-6M GPS Module Module based on U-blox NEO-6M GPS engine, incorporating regulator for 3.3-5V DC input, MS621FE-compatible rechargeable battery for backup and EEPROM for storing configuration settings. Links: NEO-6 series product information page NEO-6 Datasheet
